# Fritzing sketch wirePi_LED_bb (saved by Fritzing 0.9.4)
breadboards: 1

parts:
  Raspberry_Pi_1 = Raspberry Pi 3 [part_number=RPI-3-V1.2]
  LED1 = LED - 5mm [color="Red (633nm)" package="5 mm [THT]"]
  LED3 = LED - 5mm [color="Green (555nm)" package="5 mm [THT]"]
  LED4 = LED - 5mm [color="Red (633nm)" package="5 mm [THT]"]
  LED5 = LED - 5mm [color="Green (555nm)" package="5 mm [THT]"]
  LED6 = LED - 5mm [color="Blue (470nm)" package="5 mm [THT]"]
  LED7 = LED - 5mm [color="Blue (470nm)" package="5 mm [THT]"]
  LED8 = LED - 5mm [color="Yellow (585nm)" package="5 mm [THT]"]
  LED9 = LED - 5mm [color="Yellow (585nm)" package="5 mm [THT]"]
  R1 = Resistor [tolerance=±1% resistance=49.9 package=THT]
  R2 = Resistor [tolerance=±1% resistance=49.9 package=THT]
  R3 = Resistor [tolerance=±1% resistance=49.9 package=THT]
  R4 = Resistor [tolerance=±1% resistance=49.9 package=THT]
  R5 = Resistor [tolerance=±1% resistance=220 package=THT]
  R6 = Resistor [tolerance=±1% resistance=220 package=THT]
  R7 = Resistor [tolerance=±1% resistance=220 package=THT]
  R8 = Resistor [tolerance=±1% resistance=220 package=THT]
  LED10 = LED - 3mm [color="Green (570nm)" package="3 mm [THT]"]
  LED11 = LED - 3mm [color="Green (570nm)" package="3 mm [THT]"]
  LED12 = LED - 3mm [color="Green (570nm)" package="3 mm [THT]"]
  LED13 = LED - 3mm [color="Green (570nm)" package="3 mm [THT]"]
  R9 = Resistor [tolerance=±1% resistance=49.9 package=THT]
  R10 = Resistor [tolerance=±1% resistance=49.9 package=THT]
  R11 = Resistor [tolerance=±1% resistance=49.9 package=THT]
  R12 = Resistor [tolerance=±1% resistance=49.9 package=THT]

nets:
  N1: Raspberry_Pi_1.GPIO4, R5.Pin_1
  N2: Raspberry_Pi_1.GPIO17, R6.Pin_1
  N3: Raspberry_Pi_1.GPIO27, R7.Pin_1
  N4: Raspberry_Pi_1.GPIO22, R8.Pin_1
  N5: Raspberry_Pi_1.GPIO5, R9.Pin_1
  N6: Raspberry_Pi_1.GPIO6, R10.Pin_1
  N7: Raspberry_Pi_1.GPIO16, R12.Pin_1
  N8: Raspberry_Pi_1.GPIO12, R11.Pin_1
  N9: Raspberry_Pi_1.GPIO25, R4.Pin_1
  N10: Raspberry_Pi_1.GPIO24, R3.Pin_1
  N11: Raspberry_Pi_1.GPIO23, R2.Pin_1
  N12: Raspberry_Pi_1.GND, LED1.cathode, LED3.cathode, LED4.cathode, LED5.cathode, LED6.cathode, LED7.cathode, LED8.cathode, LED9.cathode, LED10.cathode, LED11.cathode, LED12.cathode, LED13.cathode
  N13: Raspberry_Pi_1.GPIO18, R1.Pin_1
  N14: LED1.anode, R1.Pin_0
  N15: LED3.anode, R3.Pin_0
  N16: LED4.anode, R2.Pin_0
  N17: LED5.anode, R4.Pin_0
  N18: LED6.anode, R5.Pin_0
  N19: LED7.anode, R6.Pin_0
  N20: LED8.anode, R7.Pin_0
  N21: LED9.anode, R8.Pin_0
  N22: LED10.anode, R9.Pin_0
  N23: LED11.anode, R10.Pin_0
  N24: LED12.anode, R11.Pin_0
  N25: LED13.anode, R12.Pin_0

notes:
  Zoom in/out
  Rotate cw/ccw
  Pan up/down/left/right
  Avoid Front
  Avoid Rear
  Avoid Left
  Avoid Right
